# Fritzing sketch Diagrama_Eletrico (saved by Fritzing 0.9.3b)

parts:
  Componente1 = Arduino Uno (Rev3)  # not connected
  Componente2 = AF_mshield-v1.2_breadboard
  M1 = Getriebemotor
  M2 = Getriebemotor
  M3 = Getriebemotor
  M4 = Getriebemotor
  VCC1 = Battery
  hc-sr1 = hc-sr04
  S1 = Toggle Switch [package=THT]
  A1 = ky-033 [package=THT]
  A2 = ky-033 [package=THT]

nets:
  N1: Componente2.V+, Componente2.9V, VCC1.+
  GND: Componente2.GND, hc-sr1.GND, S1.COM, A1.pin3, A2.pin3
  VCC: Componente2.VCC, hc-sr1.VCC, A1.pin4, A2.pin4
  N2: Componente2.3, hc-sr1.Trig
  N3: Componente2.4, hc-sr1.Echo
  N4: Componente2.5, A2.pin2
  N5: Componente2.6, A1.pin2
  N6: Componente2.P1#166, M1.pin_2
  N7: Componente2.P2#167, M1.pin_1
  N8: Componente2.P4#169, M4.pin_2
  N9: Componente2.P5#170, M4.pin_1
  N10: Componente2.P1#171, M3.pin_2
  N11: Componente2.P2#172, M3.pin_1
  N12: Componente2.P4#174, M2.pin_2
  N13: Componente2.P5#175, M2.pin_1
  N14: VCC1.-, S1.L2

custom parts:
  : motor Shield v1 Adafruit Adafruit Motor/Stepper/Servo Shield for Arduino kit [v1.2] : ID 81 : $19.50 : Adafruit Industries, Unique & fun DIY electronics and kits
  Battery: Your standard 2x 18650 battery pack (7.4 Volts)
  ky-033: KY-033 Line successor module with TCRT5000 and analog output.
